# Fritzing sketch wiring (saved by Fritzing 0.9.10b)

parts:
  Mod1 = Amica NodeMCU DEVKIT 1.0
  Bauteil1 = Triple Axis Accelerometer Breakout - ADXL345
  J1 = Basic Servo
  BAT1 = Battery Holders [package=lipo-1100mAh]
  U1 = SWITCH_SPDT [package=kps-1290]

nets:
  VCC: Mod1.pin1, Mod1.pin_26, Bauteil1.VCC, J1.vcc
  GND: Mod1.pin2, Mod1.pin_29, Bauteil1.GND, J1.gnd, BAT1.-
  N1: Mod1.pin_12, J1.pulse
  N2: Mod1.pin_13, Bauteil1.SCL
  N3: Mod1.pin_14, Bauteil1.SDA
  N4: Mod1.pin_30, U1.S
  N5: BAT1.+, U1.P
